# Fritzing sketch FART Sensor (saved by Fritzing 1.0.4)
breadboards: 1

parts:
  A1 = XIAO NRF52840 sense tht
  Reset = Pushbutton [package="[SMD]"]
  R1 = Resistor [tolerance=±0.1% resistance=10k package="0805 [SMD]"]
  R2 = Resistor [tolerance=±0.1% resistance=10k package="0805 [SMD]"]
  R3 = Temperature Sensor (Thermistor) [thermistor_type=NTC package=THT]
  R4 = Temperature Sensor (Thermistor) [thermistor_type=NTC package=THT]

nets:
  N1: A1.Pin_6, R1.Pin_0, R3.pin_1
  N2: A1.Pin_7, R1.Pin_1, R2.Pin_0
  N3: A1.Pin_8, R2.Pin_1, R4.pin_0
  N4: A1.Pin_17, Reset.Pin_3, Reset.Pin_4
  N5: A1.Pin_20, Reset.Pin_1, Reset.Pin_2
  N6: A1.Pin_21, R3.pin_0, R4.pin_1

custom parts:
  XIAO NRF52840 sense tht: The Seeed Studio XIAO family, Seeed Studio XIAO nRF52840 is equipped with a powerful Nordic nRF52840 MCU which integrates Bluetooth 5.0 connectivity. This is the THT version there is also a SMD version of the part.
